# Fritzing sketch final fritzing (saved by Fritzing 0.9.5d)
breadboards: 1

parts:
  U1 = ESP32-38PinWide [part_number=ESP32-38PinWide]
  M1 = fc-51 [package=THT]
  M2 = fc-51 [package=THT]
  M3 = fc-51 [package=THT]
  M4 = fc-51 [package=THT]
  Part1 = LCD1602-I2C
  J1 = Piezo Speaker
  LED1 = LED - 5mm [color="Red (633nm)" package="5 mm [THT]"]
  R1 = Resistor [tolerance=±5% resistance=220 package=THT]
  T1 = LM35 Temperature Sensor [package="TO92 [THT]"]
  module1 = MQ-2 Gas Sensor
  Matrix_keypad1 = KEYPAD 4x4

nets:
  VCC: U1.3.3, U1.VIN, M1.pin3, M2.pin3, M3.pin3, M4.pin3, Part1.VCC, R1.Pin_1, T1.+Vs, module1.VCC
  N1: U1.GPIO36, T1.Vout
  N2: U1.GPIO39, module1.AO
  N3: U1.GPIO34, M1.pin1
  N4: U1.GPIO35, M2.pin1
  N5: U1.GPIO32, M3.pin1
  N6: U1.GPIO33, M4.pin1
  N7: U1.GPIO25, Matrix_keypad1.col3
  N8: U1.GPIO26, Matrix_keypad1.col4
  N9: U1.GPIO12, Matrix_keypad1.col1
  GND: U1.GND, M1.pin2, M2.pin2, M3.pin2, M4.pin2, Part1.GND, J1.pin1, LED1.cathode, T1.GND, module1.GND
  N10: U1.GPIO13, Matrix_keypad1.col2
  N11: U1.GPIO2, LED1.anode, R1.Pin_0
  N12: U1.GPIO4, J1.pin2
  N13: U1.GPIO5, Matrix_keypad1.row3
  N14: U1.GPIO18, Matrix_keypad1.row1
  N15: U1.GPIO19, Matrix_keypad1.row2
  N16: U1.GPIO21, Part1.SDA
  N17: U1.GPIO22, Part1.SCL
  N18: U1.GPIO23, Matrix_keypad1.row4

custom parts:
  ESP32-38PinWide: Generic 38-Pin ESP32 with wide format (only access to one side of pins on a breadboard) based on Stephen Lilley's HiLetgo ESP-WROOM-32 ESP32 ESP-32S Development Board.
  fc-51: Fc-51 Infrared Obstacle Avoidance Proximity Sensor module. IR transmitter led, receiver LED, lm393 compaitor and a pot. 3.3 V to 5V power.
  LCD1602-I2C: A standard character display, usually with 2x16 characters. Comes in many colors with LCM1602 IIC attached.
  MQ-2 Gas Sensor: MQ-2 Gas Sensor module of ZHIYU Sensor Kit
  KEYPAD 4x4: Matrix keypad 16 buttons, 4 rows x 4 columns
